# Fritzing sketch teensy-joystick (saved by Fritzing 0.9.3b)
circuit board: 8.46667cm x 5.64444cm
breadboards: 1

parts:
  Teensy1 = Teensy 2.0
  R1 = Rotary Potentiometer (Large) [maximum_resistance=100kΩ package=THT]
  S1 = Momentary Switch [package=ksa_sealed_tac_switch]

nets:
  N1: Teensy1.GND, R1.leg2, S1.1, S1.2
  N2: Teensy1.D7, S1.3, S1.4
  N3: Teensy1.F0, R1.wiper
  N4: Teensy1.VCC, R1.leg1
